// Logisim project mips_pipeline.circ as structural Verilog: 15 circuits, main circuit main
module main (
);

  wire branchdecider_1_branch, clock_1_out, hazardunit_1_bubble, hazardunit_1_stallid, hazardunit_1_stallpc,
       not_1_out, not_2_out, or_1_out, or_2_out, reg_ex_mem_1_bne_2, reg_ex_mem_1_branch_2,
       reg_ex_mem_1_jal_2, reg_ex_mem_1_memory_write_2, reg_ex_mem_1_memtoreg_2, reg_ex_mem_1_regwrite_2,
       reg_ex_mem_1_zero_2, reg_id_ex_1_alusrc_2, reg_id_ex_1_bne_2, reg_id_ex_1_branch_2, reg_id_ex_1_jal_2,
       reg_id_ex_1_jr_2, reg_id_ex_1_jump_2, reg_id_ex_1_memtoreg_2, reg_id_ex_1_memwrite_2,
       reg_id_ex_1_readrs_2, reg_id_ex_1_readrt_2, reg_id_ex_1_regdest_2, reg_id_ex_1_regwrite_2,
       reg_id_ex_1_shift_2, reg_mem_wb_1_jal_2, reg_mem_wb_1_memtoreg_2, reg_mem_wb_1_reg_write_2,
       uc_w_1_alusrc, uc_w_1_bne, uc_w_1_branch, uc_w_1_jal, uc_w_1_jr, uc_w_1_jump, uc_w_1_memtoreg,
       uc_w_1_memwrite, uc_w_1_readrs, uc_w_1_readrt, uc_w_1_regdest, uc_w_1_regwrite, uc_w_1_shift,
       ula_1_igual;
  wire [1:0] hazardunit_1_rsoutput, hazardunit_1_rtoutput;
  wire [3:0] reg_id_ex_1_aluop_2, uc_w_1_aluop;
  wire [4:0] multiplexer_6_out, multiplexer_7_out, reg_ex_mem_1_write_register_2, reg_id_ex_1_rd_2,
       reg_id_ex_1_rs_2, reg_id_ex_1_rt_2, reg_mem_wb_1_write_register_2;
  wire [5:0] alu_control_1_out_3, reg_id_ex_1_imext_2;
  wire [31:0] adder_1_out, adder_2_out, banco_registradores_1_r1, banco_registradores_1_r2,
       bit_extender_1_out, DATA_MEMORY_data, INSTRUCTION_MEMORY_data, multiplexer_1_out, multiplexer_2_out,
       multiplexer_3_out, multiplexer_4_out, multiplexer_5_out, multiplexer_8_out, multiplexer_9_out,
       multiplexer_10_out, multiplexer_11_out, PC_q, reg_ex_mem_1_alu_out_2, reg_ex_mem_1_branch_address_2,
       reg_ex_mem_1_data_rt_2, reg_ex_mem_1_pc_4_2, reg_id_ex_1_data_rs_2, reg_id_ex_1_data_rt_2,
       reg_id_ex_1_jumpaddr_2, reg_id_ex_1_pc_4_2, reg_if_id_1_out_5, reg_if_id_1_out_6,
       reg_mem_wb_1_alu_out_2, reg_mem_wb_1_mem_out_2, reg_mem_wb_1_pc_4_2, shifter_1_out, ula_1_resultado;
  wire [31:6] reg_id_ex_1_imext_2_2;

  Multiplexer #(.width(32), .enable("false")) multiplexer_1 (
    .in0(adder_1_out), .in1(reg_id_ex_1_data_rs_2), .out(multiplexer_1_out), .sel(reg_id_ex_1_jr_2));
  Multiplexer #(.width(32), .enable("false")) multiplexer_2 (
    .in0(multiplexer_1_out), .in1(reg_id_ex_1_jumpaddr_2), .out(multiplexer_2_out), .sel(or_1_out));
  Multiplexer #(.width(32), .enable("false")) multiplexer_3 (
    .in0(multiplexer_2_out), .in1(reg_ex_mem_1_branch_address_2), .out(multiplexer_3_out),
    .sel(branchdecider_1_branch));
  Register #(.width(32), .Select("low")) PC (
    .D(multiplexer_3_out), .en(not_2_out), .Q(PC_q), .clk(clock_1_out));  // open: clr
  Adder #(.width(32)) adder_1 (.a(PC_q), .b(32'h4), .out(adder_1_out));  // open: cin, cout
  REG_IF_ID reg_if_id_1 (
    .in_1(adder_1_out), .in_2(INSTRUCTION_MEMORY_data), .out_5(reg_if_id_1_out_5), .out_6(reg_if_id_1_out_6),
    .CLK(clock_1_out), .Enable(not_1_out));
  RAM #(.addrWidth(16), .dataWidth(32), .Select("high"), .simpleMode("false")) INSTRUCTION_MEMORY (
    .addr(PC_q[17:2]), .data(INSTRUCTION_MEMORY_data), .clk(clock_1_out));  // open: sel, ld, clr
  assign bit_extender_1_out = {{16{reg_if_id_1_out_6[15]}}, reg_if_id_1_out_6[15:0]};  // Bit_Extender bit_extender_1
  UC_W uc_w_1 (
    .in_1(reg_if_id_1_out_6[31:26]), .REGDEST(uc_w_1_regdest), .BNE(uc_w_1_bne), .BRANCH(uc_w_1_branch),
    .ALUOP(uc_w_1_aluop), .MEMWRITE(uc_w_1_memwrite), .ALUSRC(uc_w_1_alusrc), .REGWRITE(uc_w_1_regwrite),
    .JUMP(uc_w_1_jump), .JAL(uc_w_1_jal), .in_2(reg_if_id_1_out_6[5:0]), .ReadRS(uc_w_1_readrs),
    .ReadRT(uc_w_1_readrt), .JR(uc_w_1_jr), .Shift(uc_w_1_shift), .MEMTOREG(uc_w_1_memtoreg));
  not not_1 (not_1_out, hazardunit_1_stallid);
  not not_2 (not_2_out, hazardunit_1_stallpc);
  banco_registradores banco_registradores_1 (
    .R1_num(reg_if_id_1_out_6[25:21]), .R2_num(reg_if_id_1_out_6[20:16]), .RW(reg_mem_wb_1_write_register_2),
    .Din(multiplexer_11_out), .WE(reg_mem_wb_1_reg_write_2), .clk(clock_1_out),
    .R1(banco_registradores_1_r1), .R2(banco_registradores_1_r2));
  Clock clock_1 (.out(clock_1_out));
  or or_1 (or_1_out, reg_id_ex_1_jump_2, reg_id_ex_1_jal_2);
  REG_ID_EX reg_id_ex_1 (
    .RegDest(uc_w_1_regdest), .Branch(uc_w_1_branch), .MemtoReg(uc_w_1_memtoreg), .ALUOp(uc_w_1_aluop),
    .ALUSrc(uc_w_1_alusrc), .RegWrite(uc_w_1_regwrite), .PC_4(reg_if_id_1_out_5),
    .DATA_RS(banco_registradores_1_r1), .DATA_RT(banco_registradores_1_r2), .IMEXT(bit_extender_1_out),
    .RT(reg_if_id_1_out_6[20:16]), .RD(reg_if_id_1_out_6[15:11]), .RegDest_2(reg_id_ex_1_regdest_2),
    .Branch_2(reg_id_ex_1_branch_2), .MemtoReg_2(reg_id_ex_1_memtoreg_2), .ALUOp_2(reg_id_ex_1_aluop_2),
    .ALUSrc_2(reg_id_ex_1_alusrc_2), .RegWrite_2(reg_id_ex_1_regwrite_2), .PC_4_2(reg_id_ex_1_pc_4_2),
    .DATA_RS_2(reg_id_ex_1_data_rs_2), .DATA_RT_2(reg_id_ex_1_data_rt_2),
    .IMEXT_2({reg_id_ex_1_imext_2_2, reg_id_ex_1_imext_2}), .RT_2(reg_id_ex_1_rt_2), .RD_2(reg_id_ex_1_rd_2),
    .CLK(clock_1_out), .MemWrite(uc_w_1_memwrite), .MemWrite_2(reg_id_ex_1_memwrite_2), .BNE(uc_w_1_bne),
    .BNE_2(reg_id_ex_1_bne_2), .JR(uc_w_1_jr), .JR_2(reg_id_ex_1_jr_2), .JAL(uc_w_1_jal),
    .JAL_2(reg_id_ex_1_jal_2), .Shift(uc_w_1_shift), .Shift_2(reg_id_ex_1_shift_2),
    .JUMPADDR({reg_if_id_1_out_5[31:28], reg_if_id_1_out_6[25:0], 2'b00}),
    .JUMPADDR_2(reg_id_ex_1_jumpaddr_2), .JUMP(uc_w_1_jump), .JUMP_2(reg_id_ex_1_jump_2),
    .ReadRS(uc_w_1_readrs), .ReadRS_2(reg_id_ex_1_readrs_2), .ReadRT(uc_w_1_readrt),
    .ReadRT_2(reg_id_ex_1_readrt_2), .RS(reg_if_id_1_out_6[25:21]), .RS_2(reg_id_ex_1_rs_2),
    .Stall(hazardunit_1_bubble));
  HazardUnit hazardunit_1 (
    .RSOutput(hazardunit_1_rsoutput), .RTOutput(hazardunit_1_rtoutput), .RS_EX(reg_id_ex_1_rs_2),
    .RT_EX(reg_id_ex_1_rt_2), .RegDMem(reg_ex_mem_1_write_register_2),
    .RegDWb(reg_mem_wb_1_write_register_2), .ReadRS_EX(reg_id_ex_1_readrs_2),
    .ReadRT_EX(reg_id_ex_1_readrt_2), .RegWriteMem(reg_ex_mem_1_regwrite_2),
    .RegWriteWb(reg_mem_wb_1_reg_write_2), .RS_ID(reg_if_id_1_out_6[25:21]),
    .RT_ID(reg_if_id_1_out_6[20:16]), .isLW(reg_id_ex_1_memtoreg_2), .ReadRS_ID(uc_w_1_readrs),
    .ReadRT_ID(uc_w_1_readrt), .Bubble(hazardunit_1_bubble), .StallID(hazardunit_1_stallid),
    .StallPC(hazardunit_1_stallpc));
  Multiplexer #(.select(2), .width(32), .enable("false")) multiplexer_4 (
    .in0(reg_id_ex_1_data_rs_2), .in1(reg_ex_mem_1_alu_out_2), .in2(multiplexer_11_out),
    .out(multiplexer_4_out), .sel(hazardunit_1_rsoutput));  // open: in3
  Multiplexer #(.select(2), .width(32), .enable("false")) multiplexer_5 (
    .in0(reg_id_ex_1_data_rt_2), .in1(reg_ex_mem_1_alu_out_2), .in2(multiplexer_11_out),
    .out(multiplexer_5_out), .sel(hazardunit_1_rtoutput));  // open: in3
  or or_2 (or_2_out, reg_id_ex_1_shift_2, reg_id_ex_1_alusrc_2);
  Multiplexer #(.width(5), .enable("false")) multiplexer_6 (
    .in0(reg_id_ex_1_rt_2), .in1(reg_id_ex_1_rd_2), .out(multiplexer_6_out), .sel(reg_id_ex_1_regdest_2));
  Multiplexer #(.width(5), .enable("false")) multiplexer_7 (
    .in0(multiplexer_6_out), .in1({5{1'b1}}), .out(multiplexer_7_out), .sel(reg_id_ex_1_jal_2));
  Multiplexer #(.width(32), .enable("false")) multiplexer_8 (
    .in0(multiplexer_4_out), .in1(multiplexer_5_out), .out(multiplexer_8_out), .sel(reg_id_ex_1_shift_2));
  Multiplexer #(.width(32), .enable("false")) multiplexer_9 (
    .in0(multiplexer_5_out), .in1({reg_id_ex_1_imext_2_2, reg_id_ex_1_imext_2}), .out(multiplexer_9_out),
    .sel(or_2_out));
  ALU_CONTROL alu_control_1 (.in_2(reg_id_ex_1_imext_2), .out_3(alu_control_1_out_3), .in_1(reg_id_ex_1_aluop_2));
  ULA ula_1 (
    .A(multiplexer_8_out), .B(multiplexer_9_out), .Resultado(ula_1_resultado), .OP(alu_control_1_out_3),
    .igual(ula_1_igual));
  Shifter #(.width(32)) shifter_1 (
    .in({reg_id_ex_1_imext_2_2, reg_id_ex_1_imext_2}), .\dist (5'b00010), .out(shifter_1_out));
  Adder #(.width(32)) adder_2 (.a(shifter_1_out), .b(reg_id_ex_1_pc_4_2), .out(adder_2_out));  // open: cin, cout
  REG_EX_MEM reg_ex_mem_1 (
    .BRANCH(reg_id_ex_1_branch_2), .MEMTOREG(reg_id_ex_1_memtoreg_2), .MEMORY_WRITE(reg_id_ex_1_memwrite_2),
    .REGWRITE(reg_id_ex_1_regwrite_2), .BRANCH_ADDRESS(adder_2_out), .zero(ula_1_igual),
    .ALU_OUT(ula_1_resultado), .DATA_RT(multiplexer_5_out), .WRITE_REGISTER(multiplexer_7_out),
    .BRANCH_2(reg_ex_mem_1_branch_2), .MEMTOREG_2(reg_ex_mem_1_memtoreg_2),
    .MEMORY_WRITE_2(reg_ex_mem_1_memory_write_2), .REGWRITE_2(reg_ex_mem_1_regwrite_2),
    .BRANCH_ADDRESS_2(reg_ex_mem_1_branch_address_2), .zero_2(reg_ex_mem_1_zero_2),
    .ALU_OUT_2(reg_ex_mem_1_alu_out_2), .DATA_RT_2(reg_ex_mem_1_data_rt_2),
    .WRITE_REGISTER_2(reg_ex_mem_1_write_register_2), .CLK(clock_1_out), .BNE(reg_id_ex_1_bne_2),
    .BNE_2(reg_ex_mem_1_bne_2), .JAL(reg_id_ex_1_jal_2), .JAL_2(reg_ex_mem_1_jal_2),
    .PC_4(reg_id_ex_1_pc_4_2), .PC_4_2(reg_ex_mem_1_pc_4_2));
  BranchDecider branchdecider_1 (
    .BEQ(reg_ex_mem_1_branch_2), .BNE(reg_ex_mem_1_bne_2), .EQ(reg_ex_mem_1_zero_2),
    .Branch(branchdecider_1_branch));
  RAM #(.addrWidth(16), .dataWidth(32), .bus("separate"), .Select("high"), .simpleMode("false")) DATA_MEMORY (
    .addr(reg_ex_mem_1_alu_out_2[17:2]), .din(reg_ex_mem_1_data_rt_2), .data(DATA_MEMORY_data),
    .str(reg_ex_mem_1_memory_write_2), .clk(clock_1_out));  // open: sel, ld, clr
  REG_MEM_WB reg_mem_wb_1 (
    .REG_WRITE(reg_ex_mem_1_regwrite_2), .MEMTOREG(reg_ex_mem_1_memtoreg_2), .MEM_OUT(DATA_MEMORY_data),
    .ALU_OUT(reg_ex_mem_1_alu_out_2), .WRITE_REGISTER(reg_ex_mem_1_write_register_2),
    .REG_WRITE_2(reg_mem_wb_1_reg_write_2), .MEMTOREG_2(reg_mem_wb_1_memtoreg_2),
    .MEM_OUT_2(reg_mem_wb_1_mem_out_2), .ALU_OUT_2(reg_mem_wb_1_alu_out_2),
    .WRITE_REGISTER_2(reg_mem_wb_1_write_register_2), .CLK(clock_1_out), .JAL(reg_ex_mem_1_jal_2),
    .JAL_2(reg_mem_wb_1_jal_2), .PC_4(reg_ex_mem_1_pc_4_2), .PC_4_2(reg_mem_wb_1_pc_4_2));
  Multiplexer #(.width(32), .enable("false")) multiplexer_10 (
    .in0(reg_mem_wb_1_alu_out_2), .in1(reg_mem_wb_1_mem_out_2), .out(multiplexer_10_out),
    .sel(reg_mem_wb_1_memtoreg_2));
  Multiplexer #(.width(32), .enable("false")) multiplexer_11 (
    .in0(multiplexer_10_out), .in1(reg_mem_wb_1_pc_4_2), .out(multiplexer_11_out), .sel(reg_mem_wb_1_jal_2));

  // Notes on the sheet:
  //   OPCode
  //   Funct
  //   RS
  //   RT
  //   RD
  //   PC + 4
  //   IMMExt
  //   JumpADDR
  //   Jump
  //   JR
  //   JAL
  //   BNE
  //   Branch
  //   MemtoReg
  //   MemWrite
  //   RegWrite
  //   Shift
  //   ALUSrc
  //   RegDest
  //   ALUOp
  //   ReadRS
  //   ReadRT
endmodule

module banco_registradores (
  input  [4:0] R1_num,
  input  [4:0] R2_num,
  input  [4:0] RW,
  input  [31:0] Din,
  input  WE,
  input  clk,
  output [31:0] R1,
  output [31:0] R2
);

  wire demultiplexer_1_out0, demultiplexer_1_out1, demultiplexer_1_out2, demultiplexer_1_out3,
       demultiplexer_2_out0, demultiplexer_2_out1, demultiplexer_2_out2, demultiplexer_2_out3,
       demultiplexer_2_out4, demultiplexer_2_out5, demultiplexer_2_out6, demultiplexer_2_out7,
       demultiplexer_3_out0, demultiplexer_3_out1, demultiplexer_3_out2, demultiplexer_3_out3,
       demultiplexer_3_out4, demultiplexer_3_out5, demultiplexer_3_out6, demultiplexer_3_out7,
       demultiplexer_4_out0, demultiplexer_4_out1, demultiplexer_4_out2, demultiplexer_4_out3,
       demultiplexer_4_out4, demultiplexer_4_out5, demultiplexer_4_out6, demultiplexer_4_out7,
       demultiplexer_5_out0, demultiplexer_5_out1, demultiplexer_5_out2, demultiplexer_5_out3,
       demultiplexer_5_out4, demultiplexer_5_out5, demultiplexer_5_out6, demultiplexer_5_out7;
  wire [31:0] _0__Zero_q, _1__at_q, _3__v1_q, _5__a1_q, _6__a2_q, _7__a3_q, _8__t0_q, _9__t1_q, _10__t2_q,
       _11__t3_q, _12__t4_q, _13__t5_q, _14__t6_q, _15__t7_q, _19__s3_q, _20__s4_q, _21__s5_q, _22__s6_q,
       _23__s7_q, _24__t8_q, _25__t9_q, _26__k0_q, _27__k1_q, _28__gp_q, _29__sp_q, _30__fp_q, a0, ra, s0,
       s1, s2, v0;

  Demultiplexer #(.select(2), .disabled(0)) demultiplexer_1 (
    .out0(demultiplexer_1_out0), .out1(demultiplexer_1_out1), .out2(demultiplexer_1_out2),
    .out3(demultiplexer_1_out3), .in(1'b1), .sel(RW[4:3]), .en(WE));
  Demultiplexer #(.select(3), .disabled(0)) demultiplexer_2 (
    .out0(demultiplexer_2_out0), .out1(demultiplexer_2_out1), .out2(demultiplexer_2_out2),
    .out3(demultiplexer_2_out3), .out4(demultiplexer_2_out4), .out5(demultiplexer_2_out5),
    .out6(demultiplexer_2_out6), .out7(demultiplexer_2_out7), .in(1'b1), .sel(RW[2:0]),
    .en(demultiplexer_1_out0));
  Demultiplexer #(.select(3), .disabled(0)) demultiplexer_3 (
    .out0(demultiplexer_3_out0), .out1(demultiplexer_3_out1), .out2(demultiplexer_3_out2),
    .out3(demultiplexer_3_out3), .out4(demultiplexer_3_out4), .out5(demultiplexer_3_out5),
    .out6(demultiplexer_3_out6), .out7(demultiplexer_3_out7), .in(1'b1), .sel(RW[2:0]),
    .en(demultiplexer_1_out1));
  Demultiplexer #(.select(3), .disabled(0)) demultiplexer_4 (
    .out0(demultiplexer_4_out0), .out1(demultiplexer_4_out1), .out2(demultiplexer_4_out2),
    .out3(demultiplexer_4_out3), .out4(demultiplexer_4_out4), .out5(demultiplexer_4_out5),
    .out6(demultiplexer_4_out6), .out7(demultiplexer_4_out7), .in(1'b1), .sel(RW[2:0]),
    .en(demultiplexer_1_out2));
  Demultiplexer #(.select(3), .disabled(0)) demultiplexer_5 (
    .out0(demultiplexer_5_out0), .out1(demultiplexer_5_out1), .out2(demultiplexer_5_out2),
    .out3(demultiplexer_5_out3), .out4(demultiplexer_5_out4), .out5(demultiplexer_5_out5),
    .out6(demultiplexer_5_out6), .out7(demultiplexer_5_out7), .in(1'b1), .sel(RW[2:0]),
    .en(demultiplexer_1_out3));
  Register #(.width(32), .Select("low")) _0__Zero (
    .D(Din), .en(demultiplexer_2_out0), .Q(_0__Zero_q));  // open: clk, clr
  Register #(.width(32), .Select("low")) _8__t0 (
    .D(Din), .en(demultiplexer_3_out0), .Q(_8__t0_q), .clk(clk));  // open: clr
  Register #(.width(32), .Select("low")) _16__s0 (.D(Din), .en(demultiplexer_4_out0), .Q(s0), .clk(clk));  // open: clr
  Register #(.width(32), .Select("low")) _24__t8 (
    .D(Din), .en(demultiplexer_5_out0), .Q(_24__t8_q), .clk(clk));  // open: clr
  Register #(.width(32), .Select("low")) _1__at (
    .D(Din), .en(demultiplexer_2_out1), .Q(_1__at_q), .clk(clk));  // open: clr
  Register #(.width(32), .Select("low")) _9__t1 (
    .D(Din), .en(demultiplexer_3_out1), .Q(_9__t1_q), .clk(clk));  // open: clr
  Register #(.width(32), .Select("low")) _17__s1 (.D(Din), .en(demultiplexer_4_out1), .Q(s1), .clk(clk));  // open: clr
  Register #(.width(32), .Select("low")) _25__t9 (
    .D(Din), .en(demultiplexer_5_out1), .Q(_25__t9_q), .clk(clk));  // open: clr
  Register #(.width(32), .Select("low")) _2__v0 (.D(Din), .en(demultiplexer_2_out2), .Q(v0), .clk(clk));  // open: clr
  Register #(.width(32), .Select("low")) _10__t2 (
    .D(Din), .en(demultiplexer_3_out2), .Q(_10__t2_q), .clk(clk));  // open: clr
  Register #(.width(32), .Select("low")) _18__s2 (.D(Din), .en(demultiplexer_4_out2), .Q(s2), .clk(clk));  // open: clr
  Register #(.width(32), .Select("low")) _26__k0 (
    .D(Din), .en(demultiplexer_5_out2), .Q(_26__k0_q), .clk(clk));  // open: clr
  Register #(.width(32), .Select("low")) _3__v1 (
    .D(Din), .en(demultiplexer_2_out3), .Q(_3__v1_q), .clk(clk));  // open: clr
  Register #(.width(32), .Select("low")) _11__t3 (
    .D(Din), .en(demultiplexer_3_out3), .Q(_11__t3_q), .clk(clk));  // open: clr
  Register #(.width(32), .Select("low")) _19__s3 (
    .D(Din), .en(demultiplexer_4_out3), .Q(_19__s3_q), .clk(clk));  // open: clr
  Register #(.width(32), .Select("low")) _27__k1 (
    .D(Din), .en(demultiplexer_5_out3), .Q(_27__k1_q), .clk(clk));  // open: clr
  Register #(.width(32), .Select("low")) _4__a0 (.D(Din), .en(demultiplexer_2_out4), .Q(a0), .clk(clk));  // open: clr
  Register #(.width(32), .Select("low")) _12__t4 (
    .D(Din), .en(demultiplexer_3_out4), .Q(_12__t4_q), .clk(clk));  // open: clr
  Register #(.width(32), .Select("low")) _20__s4 (
    .D(Din), .en(demultiplexer_4_out4), .Q(_20__s4_q), .clk(clk));  // open: clr
  Register #(.width(32), .Select("low")) _28__gp (
    .D(Din), .en(demultiplexer_5_out4), .Q(_28__gp_q), .clk(clk));  // open: clr
  Register #(.width(32), .Select("low")) _5__a1 (
    .D(Din), .en(demultiplexer_2_out5), .Q(_5__a1_q), .clk(clk));  // open: clr
  Register #(.width(32), .Select("low")) _13__t5 (
    .D(Din), .en(demultiplexer_3_out5), .Q(_13__t5_q), .clk(clk));  // open: clr
  Register #(.width(32), .Select("low")) _21__s5 (
    .D(Din), .en(demultiplexer_4_out5), .Q(_21__s5_q), .clk(clk));  // open: clr
  Register #(.width(32), .Select("low")) _29__sp (
    .D(Din), .en(demultiplexer_5_out5), .Q(_29__sp_q), .clk(clk));  // open: clr
  Register #(.width(32), .Select("low")) _6__a2 (
    .D(Din), .en(demultiplexer_2_out6), .Q(_6__a2_q), .clk(clk));  // open: clr
  Register #(.width(32), .Select("low")) _14__t6 (
    .D(Din), .en(demultiplexer_3_out6), .Q(_14__t6_q), .clk(clk));  // open: clr
  Register #(.width(32), .Select("low")) _22__s6 (
    .D(Din), .en(demultiplexer_4_out6), .Q(_22__s6_q), .clk(clk));  // open: clr
  Register #(.width(32), .Select("low")) _30__fp (
    .D(Din), .en(demultiplexer_5_out6), .Q(_30__fp_q), .clk(clk));  // open: clr
  Register #(.width(32), .Select("low")) _7__a3 (
    .D(Din), .en(demultiplexer_2_out7), .Q(_7__a3_q), .clk(clk));  // open: clr
  Register #(.width(32), .Select("low")) _15__t7 (
    .D(Din), .en(demultiplexer_3_out7), .Q(_15__t7_q), .clk(clk));  // open: clr
  Register #(.width(32), .Select("low")) _23__s7 (
    .D(Din), .en(demultiplexer_4_out7), .Q(_23__s7_q), .clk(clk));  // open: clr
  Register #(.width(32), .Select("low")) _31__ra (.D(Din), .en(demultiplexer_5_out7), .Q(ra), .clk(clk));  // open: clr
  Multiplexer #(.select(5), .width(32), .enable("false")) multiplexer_1 (
    .in0(_0__Zero_q), .in1(_1__at_q), .in2(v0), .in3(_3__v1_q), .in4(a0), .in5(_5__a1_q), .in6(_6__a2_q),
    .in7(_7__a3_q), .in8(_8__t0_q), .in9(_9__t1_q), .in10(_10__t2_q), .in11(_11__t3_q), .in12(_12__t4_q),
    .in13(_13__t5_q), .in14(_14__t6_q), .in15(_15__t7_q), .in16(s0), .in17(s1), .in18(s2), .in19(_19__s3_q),
    .in20(_20__s4_q), .in21(_21__s5_q), .in22(_22__s6_q), .in23(_23__s7_q), .in24(_24__t8_q),
    .in25(_25__t9_q), .in26(_26__k0_q), .in27(_27__k1_q), .in28(_28__gp_q), .in29(_29__sp_q),
    .in30(_30__fp_q), .in31(ra), .out(R1), .sel(R1_num));
  Multiplexer #(.select(5), .width(32), .enable("false")) multiplexer_2 (
    .in0(_0__Zero_q), .in1(_1__at_q), .in2(v0), .in3(_3__v1_q), .in4(a0), .in5(_5__a1_q), .in6(_6__a2_q),
    .in7(_7__a3_q), .in8(_8__t0_q), .in9(_9__t1_q), .in10(_10__t2_q), .in11(_11__t3_q), .in12(_12__t4_q),
    .in13(_13__t5_q), .in14(_14__t6_q), .in15(_15__t7_q), .in16(s0), .in17(s1), .in18(s2), .in19(_19__s3_q),
    .in20(_20__s4_q), .in21(_21__s5_q), .in22(_22__s6_q), .in23(_23__s7_q), .in24(_24__t8_q),
    .in25(_25__t9_q), .in26(_26__k0_q), .in27(_27__k1_q), .in28(_28__gp_q), .in29(_29__sp_q),
    .in30(_30__fp_q), .in31(ra), .out(R2), .sel(R2_num));

  // Other names for the same wires on the sheet: reg1[31:0] = R1; reg1_num[4:0] = R1_num; reg2[31:0] = R2;
  //   reg2_num[4:0] = R2_num; write_data[31:0] = Din; write_reg_num[4:0] = RW

  // Notes on the sheet:
  //   Input
  //   Output
endmodule

module ULA (
  input  [31:0] A,
  input  [31:0] B,
  input  [5:0] OP,
  output igual,
  output [31:0] Resultado
);

  wire [31:0] adder_1_out, and_1_out, bit_extender_1_out, divider_1_out, multiplier_1_out, or_1_out,
       shifter_1_out, shifter_2_out, subtractor_1_out, subtractor_2_out;

  Adder #(.width(32)) adder_1 (.a(A), .b(B), .out(adder_1_out));  // open: cin, cout
  Subtractor #(.width(32)) subtractor_1 (.a(A), .b(B), .out(subtractor_1_out));  // open: bin, bout
  Multiplier #(.width(32)) multiplier_1 (.a(A), .b(B), .out(multiplier_1_out));  // open: cin, cout
  Divider #(.width(32)) divider_1 (.a(A), .b(B), .out(divider_1_out));  // open: upper, rem
  Comparator #(.width(32)) comparator_1 (.a(A), .b(B), .eq(igual));  // open: gt, lt
  assign and_1_out = A & B;  // AND_Gate and_1, 32 bits wide
  assign or_1_out = A | B;  // OR_Gate or_1, 32 bits wide
  Subtractor #(.width(32)) subtractor_2 (.a(A), .b(B), .out(subtractor_2_out));  // open: bin, bout
  Shifter #(.width(32)) shifter_1 (.in(A), .\dist (B[10:6]), .out(shifter_1_out));
  Shifter #(.width(32), .shift("lr")) shifter_2 (.in(A), .\dist (B[10:6]), .out(shifter_2_out));
  assign bit_extender_1_out = {{31{1'b0}}, subtractor_2_out[31]};  // Bit_Extender bit_extender_1
  Multiplexer #(.select(4), .width(32), .enable("false")) multiplexer_1 (
    .in0(adder_1_out), .in1(subtractor_1_out), .in2(multiplier_1_out), .in3(divider_1_out), .in4(and_1_out),
    .in5(or_1_out), .in6(bit_extender_1_out), .in7(shifter_1_out), .in8(shifter_2_out), .out(Resultado),
    .sel(OP[3:0]));  // open: in9, in10, in11, in12, in13, in14, in15
endmodule

module UC (
  input  UC5,
  input  UC4,
  input  UC3,
  input  UC2,
  input  UC1,
  input  UC0,
  output REGDEST,
  output JAL,
  output JUMP,
  output BNE,
  output BRANCH,
  output MEMTOREG,
  output ULAOP2,
  output ULA0P1,
  output ULA0P0,
  output ULAOPSRC,
  output MEM_WR,
  output ULASRC,
  output WR,
  output ReadRS,
  output ReadRT,
  output ReadRegDecider
);

  wire and_1_out, and_2_out, and_9_out, and_10_out, and_11_out, and_12_out, and_13_out, and_15_out,
       and_16_out, and_17_out, and_18_out, and_20_out, and_21_out, and_22_out, and_23_out, and_24_out,
       and_25_out, and_26_out, and_27_out, and_28_out, and_29_out, and_30_out, and_31_out, and_32_out,
       and_33_out, and_34_out, and_35_out, not_1_out, not_2_out, not_3_out, not_4_out, not_5_out, not_6_out,
       not_7_out, not_8_out, not_9_out, not_10_out, not_11_out, not_12_out, not_13_out, not_14_out,
       not_15_out, not_16_out, not_17_out, not_18_out, not_19_out, not_20_out, not_21_out, not_22_out,
       not_23_out, not_24_out, not_25_out, not_26_out, not_27_out, not_28_out, not_29_out, not_30_out,
       not_31_out, not_32_out, not_33_out, not_34_out, not_35_out, not_36_out, not_37_out, not_38_out,
       not_39_out, not_40_out, not_41_out, not_42_out, not_43_out, not_44_out, not_45_out, not_46_out,
       not_47_out, not_48_out, not_49_out, not_50_out, not_51_out, not_52_out, not_53_out, not_54_out,
       not_55_out, not_56_out, not_57_out, not_58_out, not_59_out, not_60_out, not_61_out, not_62_out,
       not_63_out, not_64_out, not_65_out, not_66_out, not_67_out, not_68_out, not_69_out, not_70_out,
       not_71_out, not_72_out, not_73_out, not_74_out, not_75_out, not_76_out, not_77_out, not_78_out,
       not_79_out, not_80_out, not_81_out, not_82_out, not_83_out, not_84_out, not_85_out, not_86_out,
       not_87_out, not_88_out, not_89_out, not_90_out, not_91_out, not_92_out, not_93_out, not_94_out,
       not_95_out, not_96_out, not_97_out, not_98_out, not_99_out, not_100_out, not_101_out, not_102_out,
       not_103_out, not_104_out, not_105_out, not_106_out, not_107_out, not_108_out, not_109_out,
       not_110_out, not_111_out, not_112_out, not_113_out, not_114_out, not_115_out, not_116_out,
       not_117_out, not_118_out, not_119_out;

  not not_1 (not_1_out, UC5);
  not not_2 (not_2_out, UC4);
  not not_3 (not_3_out, UC3);
  not not_4 (not_4_out, UC2);
  not not_5 (not_5_out, UC1);
  not not_6 (not_6_out, UC0);
  not not_7 (not_7_out, UC5);
  not not_8 (not_8_out, UC4);
  not not_9 (not_9_out, UC3);
  not not_10 (not_10_out, UC1);
  not not_11 (not_11_out, UC5);
  not not_12 (not_12_out, UC4);
  not not_13 (not_13_out, UC3);
  not not_14 (not_14_out, UC2);
  not not_15 (not_15_out, UC5);
  not not_16 (not_16_out, UC4);
  not not_17 (not_17_out, UC3);
  not not_18 (not_18_out, UC2);
  not not_19 (not_19_out, UC0);
  not not_20 (not_20_out, UC5);
  not not_21 (not_21_out, UC4);
  not not_22 (not_22_out, UC3);
  not not_23 (not_23_out, UC1);
  not not_24 (not_24_out, UC5);
  not not_25 (not_25_out, UC4);
  not not_26 (not_26_out, UC3);
  not not_27 (not_27_out, UC1);
  not not_28 (not_28_out, UC0);
  not not_29 (not_29_out, UC4);
  not not_30 (not_30_out, UC3);
  not not_31 (not_31_out, UC2);
  not not_32 (not_32_out, UC5);
  not not_33 (not_33_out, UC4);
  not not_34 (not_34_out, UC2);
  not not_35 (not_35_out, UC0);
  not not_36 (not_36_out, UC5);
  not not_37 (not_37_out, UC4);
  not not_38 (not_38_out, UC3);
  not not_39 (not_39_out, UC2);
  not not_40 (not_40_out, UC1);
  not not_41 (not_41_out, UC0);
  not not_42 (not_42_out, UC5);
  not not_43 (not_43_out, UC4);
  not not_44 (not_44_out, UC3);
  not not_45 (not_45_out, UC1);
  not not_46 (not_46_out, UC5);
  not not_47 (not_47_out, UC4);
  not not_48 (not_48_out, UC2);
  not not_49 (not_49_out, UC0);
  not not_50 (not_50_out, UC5);
  not not_51 (not_51_out, UC1);
  not not_52 (not_52_out, UC5);
  not not_53 (not_53_out, UC0);
  not not_54 (not_54_out, UC5);
  not not_55 (not_55_out, UC0);
  not not_56 (not_56_out, UC5);
  not not_57 (not_57_out, UC4);
  not not_58 (not_58_out, UC2);
  not not_59 (not_59_out, UC0);
  not not_60 (not_60_out, UC5);
  not not_61 (not_61_out, UC1);
  not not_62 (not_62_out, UC5);
  not not_63 (not_63_out, UC0);
  not not_64 (not_64_out, UC4);
  not not_65 (not_65_out, UC2);
  not not_66 (not_66_out, UC4);
  not not_67 (not_67_out, UC2);
  not not_68 (not_68_out, UC5);
  not not_69 (not_69_out, UC4);
  not not_70 (not_70_out, UC2);
  not not_71 (not_71_out, UC0);
  not not_72 (not_72_out, UC5);
  not not_73 (not_73_out, UC1);
  not not_74 (not_74_out, UC5);
  not not_75 (not_75_out, UC0);
  not not_76 (not_76_out, UC4);
  not not_77 (not_77_out, UC2);
  not not_78 (not_78_out, UC5);
  not not_79 (not_79_out, UC4);
  not not_80 (not_80_out, UC2);
  not not_81 (not_81_out, UC1);
  not not_82 (not_82_out, UC0);
  not not_83 (not_83_out, UC4);
  not not_84 (not_84_out, UC3);
  not not_85 (not_85_out, UC2);
  not not_86 (not_86_out, UC5);
  not not_87 (not_87_out, UC4);
  not not_88 (not_88_out, UC2);
  not not_89 (not_89_out, UC0);
  not not_90 (not_90_out, UC5);
  not not_91 (not_91_out, UC1);
  not not_92 (not_92_out, UC5);
  not not_93 (not_93_out, UC0);
  not not_94 (not_94_out, UC5);
  not not_95 (not_95_out, UC4);
  not not_96 (not_96_out, UC3);
  not not_97 (not_97_out, UC1);
  not not_98 (not_98_out, UC5);
  not not_99 (not_99_out, UC4);
  not not_100 (not_100_out, UC2);
  not not_101 (not_101_out, UC0);
  not not_102 (not_102_out, UC5);
  not not_103 (not_103_out, UC1);
  not not_104 (not_104_out, UC5);
  not not_105 (not_105_out, UC0);
  not not_106 (not_106_out, UC4);
  not not_107 (not_107_out, UC2);
  not not_108 (not_108_out, UC5);
  not not_109 (not_109_out, UC4);
  not not_110 (not_110_out, UC3);
  not not_111 (not_111_out, UC1);
  not not_112 (not_112_out, UC4);
  not not_113 (not_113_out, UC2);
  not not_114 (not_114_out, UC5);
  not not_115 (not_115_out, UC4);
  not not_116 (not_116_out, UC3);
  not not_117 (not_117_out, UC2);
  not not_118 (not_118_out, UC1);
  not not_119 (not_119_out, UC0);
  and and_1 (and_1_out, not_1_out, not_2_out, not_3_out, not_4_out, not_5_out, not_6_out);
  and and_2 (and_2_out, not_7_out, not_8_out, not_9_out, UC2, not_10_out, UC0);
  and and_3 (JAL, not_11_out, not_12_out, not_13_out, not_14_out, UC1, UC0);
  and and_4 (JUMP, not_15_out, not_16_out, not_17_out, not_18_out, UC1, not_19_out);
  and and_5 (BNE, not_20_out, not_21_out, not_22_out, UC2, not_23_out, UC0);
  and and_6 (BRANCH, not_24_out, not_25_out, not_26_out, UC2, not_27_out, not_28_out);
  and and_7 (MEMTOREG, UC5, not_29_out, not_30_out, not_31_out, UC1, UC0);
  and and_8 (ULAOP2, not_32_out, not_33_out, UC3, not_34_out, UC1, not_35_out);
  and and_9 (and_9_out, not_36_out, not_37_out, not_38_out, not_39_out, not_40_out, not_41_out);
  and and_10 (and_10_out, not_42_out, not_43_out, not_44_out, UC2, not_45_out, UC0);
  and and_11 (and_11_out, not_46_out, not_47_out, UC3, not_48_out, UC1, not_49_out);
  and and_12 (and_12_out, not_50_out, UC4, UC3, UC2, not_51_out, UC0);
  and and_13 (and_13_out, not_52_out, UC4, UC3, UC2, UC1, not_53_out);
  and and_14 (ULA0P0, not_54_out, UC4, UC3, UC2, not_55_out);
  and and_15 (and_15_out, not_56_out, not_57_out, UC3, not_58_out, UC1, not_59_out);
  and and_16 (and_16_out, not_60_out, UC4, UC3, UC2, not_61_out);
  and and_17 (and_17_out, not_62_out, UC4, UC3, UC2, not_63_out);
  and and_18 (and_18_out, UC5, not_64_out, not_65_out, UC1, UC0);
  and and_19 (MEM_WR, UC5, not_66_out, UC3, not_67_out, UC1, UC0);
  and and_20 (and_20_out, not_68_out, not_69_out, UC3, not_70_out, not_71_out);
  and and_21 (and_21_out, not_72_out, UC4, UC3, UC2, not_73_out);
  and and_22 (and_22_out, not_74_out, UC4, UC3, UC2, not_75_out);
  and and_23 (and_23_out, UC5, not_76_out, not_77_out, UC1, UC0);
  and and_24 (and_24_out, not_78_out, not_79_out, not_80_out, not_81_out, not_82_out);
  and and_25 (and_25_out, not_83_out, not_84_out, not_85_out, UC1, UC0);
  and and_26 (and_26_out, not_86_out, not_87_out, UC3, not_88_out, not_89_out);
  and and_27 (and_27_out, not_90_out, UC4, UC3, UC2, not_91_out);
  and and_28 (and_28_out, not_92_out, UC4, UC3, UC2, not_93_out);
  and and_29 (and_29_out, not_94_out, not_95_out, not_96_out, UC2, not_97_out);
  and and_30 (and_30_out, not_98_out, not_99_out, UC3, not_100_out, not_101_out);
  and and_31 (and_31_out, not_102_out, UC4, UC3, UC2, not_103_out);
  and and_32 (and_32_out, not_104_out, UC4, UC3, UC2, not_105_out);
  and and_33 (and_33_out, UC5, not_106_out, not_107_out, UC1, UC0);
  and and_34 (and_34_out, not_108_out, not_109_out, not_110_out, UC2, not_111_out);
  and and_35 (and_35_out, UC5, not_112_out, not_113_out, UC1, UC0);
  and and_36 (ReadRegDecider, not_114_out, not_115_out, not_116_out, not_117_out, not_118_out, not_119_out);
  or or_1 (REGDEST, and_1_out, and_2_out);
  or or_2 (ULA0P1, and_9_out, and_10_out, and_11_out, and_12_out, and_13_out);
  or or_3 (ULAOPSRC, and_15_out, and_16_out, and_17_out, and_18_out);
  or or_4 (ULASRC, and_20_out, and_21_out, and_22_out, and_23_out);
  or or_5 (WR, and_24_out, and_25_out, and_26_out, and_27_out, and_28_out);
  or or_6 (ReadRS, and_29_out, and_30_out, and_31_out, and_32_out, and_33_out);
  or or_7 (ReadRT, and_34_out, and_35_out);
endmodule

// ULAOP
module OPULA (
  input  ALUOP2,
  input  ALUOP1,
  input  ALUOP0,
  input  FUNC5,
  input  FUNC4,
  input  FUNC3,
  input  FUNC2,
  input  FUNC1,
  input  FUNC0,
  output ULAOP3,
  output ULAOP2,
  output ULAOP1,
  output ULAOP0
);

  wire and_2_out, and_3_out, and_4_out, and_5_out, and_6_out, and_7_out, and_8_out, and_9_out, and_10_out,
       and_11_out, not_1_out, not_2_out, not_3_out, not_4_out, not_5_out, not_6_out, not_7_out, not_8_out,
       not_9_out, not_10_out, not_11_out, not_12_out, not_13_out, not_14_out, not_15_out, not_16_out,
       not_17_out, not_18_out, not_19_out, not_20_out, not_21_out, not_22_out, not_23_out, not_24_out,
       not_25_out, not_26_out, not_27_out, not_28_out, not_29_out, not_30_out, not_31_out, not_32_out,
       not_33_out, not_34_out, not_35_out, not_36_out, not_37_out, not_38_out, not_39_out, not_40_out,
       not_41_out, not_42_out, not_43_out, not_44_out, not_45_out, not_46_out, not_47_out, not_48_out,
       not_49_out, not_50_out, not_51_out, not_52_out, not_53_out, not_54_out, not_55_out, not_56_out,
       not_57_out, not_58_out, not_59_out, not_60_out, not_61_out, not_62_out, not_63_out, not_64_out;

  not not_1 (not_1_out, ALUOP2);
  not not_2 (not_2_out, ALUOP0);
  not not_3 (not_3_out, FUNC5);
  not not_4 (not_4_out, FUNC4);
  not not_5 (not_5_out, FUNC3);
  not not_6 (not_6_out, FUNC2);
  not not_7 (not_7_out, FUNC0);
  not not_8 (not_8_out, ALUOP2);
  not not_9 (not_9_out, ALUOP0);
  not not_10 (not_10_out, FUNC5);
  not not_11 (not_11_out, FUNC4);
  not not_12 (not_12_out, FUNC3);
  not not_13 (not_13_out, FUNC2);
  not not_14 (not_14_out, FUNC1);
  not not_15 (not_15_out, FUNC0);
  not not_16 (not_16_out, ALUOP2);
  not not_17 (not_17_out, ALUOP0);
  not not_18 (not_18_out, FUNC4);
  not not_19 (not_19_out, FUNC3);
  not not_20 (not_20_out, FUNC1);
  not not_21 (not_21_out, ALUOP2);
  not not_22 (not_22_out, ALUOP0);
  not not_23 (not_23_out, FUNC4);
  not not_24 (not_24_out, FUNC2);
  not not_25 (not_25_out, FUNC0);
  not not_26 (not_26_out, ALUOP2);
  not not_27 (not_27_out, ALUOP0);
  not not_28 (not_28_out, FUNC5);
  not not_29 (not_29_out, FUNC4);
  not not_30 (not_30_out, FUNC3);
  not not_31 (not_31_out, FUNC2);
  not not_32 (not_32_out, FUNC1);
  not not_33 (not_33_out, FUNC0);
  not not_34 (not_34_out, ALUOP0);
  not not_35 (not_35_out, FUNC5);
  not not_36 (not_36_out, FUNC2);
  not not_37 (not_37_out, FUNC0);
  not not_38 (not_38_out, ALUOP2);
  not not_39 (not_39_out, ALUOP0);
  not not_40 (not_40_out, FUNC4);
  not not_41 (not_41_out, FUNC2);
  not not_42 (not_42_out, FUNC0);
  not not_43 (not_43_out, ALUOP2);
  not not_44 (not_44_out, ALUOP0);
  not not_45 (not_45_out, FUNC5);
  not not_46 (not_46_out, FUNC4);
  not not_47 (not_47_out, FUNC3);
  not not_48 (not_48_out, FUNC2);
  not not_49 (not_49_out, FUNC1);
  not not_50 (not_50_out, FUNC0);
  not not_51 (not_51_out, ALUOP0);
  not not_52 (not_52_out, FUNC5);
  not not_53 (not_53_out, FUNC2);
  not not_54 (not_54_out, FUNC0);
  not not_55 (not_55_out, ALUOP0);
  not not_56 (not_56_out, FUNC4);
  not not_57 (not_57_out, FUNC3);
  not not_58 (not_58_out, FUNC2);
  not not_59 (not_59_out, FUNC0);
  not not_60 (not_60_out, ALUOP2);
  not not_61 (not_61_out, ALUOP0);
  not not_62 (not_62_out, FUNC4);
  not not_63 (not_63_out, FUNC3);
  not not_64 (not_64_out, FUNC1);
  and and_1 (ULAOP3, not_1_out, ALUOP1, not_2_out, not_3_out, not_4_out, not_5_out, not_6_out, FUNC1, not_7_out);
  and and_2 (and_2_out, not_8_out, ALUOP1, not_9_out, not_10_out, not_11_out, not_12_out, not_13_out, not_14_out, not_15_out);
  and and_3 (and_3_out, not_16_out, ALUOP1, not_17_out, FUNC5, not_18_out, not_19_out, FUNC2, not_20_out);
  and and_4 (and_4_out, not_21_out, ALUOP1, not_22_out, FUNC5, not_23_out, FUNC3, not_24_out, FUNC1, not_25_out);
  and and_5 (and_5_out, not_26_out, ALUOP1, not_27_out, not_28_out, not_29_out, not_30_out, not_31_out, not_32_out, not_33_out);
  and and_6 (and_6_out, ALUOP1, not_34_out, not_35_out, FUNC4, FUNC3, not_36_out, not_37_out);
  and and_7 (and_7_out, not_38_out, ALUOP1, not_39_out, FUNC5, not_40_out, FUNC3, not_41_out, FUNC1, not_42_out);
  and and_8 (and_8_out, not_43_out, ALUOP1, not_44_out, not_45_out, not_46_out, not_47_out, not_48_out, not_49_out, not_50_out);
  and and_9 (and_9_out, ALUOP1, not_51_out, not_52_out, FUNC4, FUNC3, not_53_out, FUNC1, not_54_out);
  and and_10 (and_10_out, ALUOP1, not_55_out, FUNC5, not_56_out, not_57_out, not_58_out, FUNC1, not_59_out);
  and and_11 (and_11_out, not_60_out, ALUOP1, not_61_out, FUNC5, not_62_out, not_63_out, FUNC2, not_64_out, FUNC0);
  or or_1 (ULAOP2, and_2_out, and_3_out, and_4_out);
  or or_2 (ULAOP1, and_5_out, and_6_out, and_7_out);
  or or_3 (ULAOP0, and_8_out, and_9_out, and_10_out, and_11_out);
endmodule

// UC
module UC_W (
  input  [5:0] in_1,
  input  [5:0] in_2,
  output REGDEST,
  output JAL,
  output JUMP,
  output BNE,
  output BRANCH,
  output MEMTOREG,
  output [3:0] ALUOP,
  output MEMWRITE,
  output ALUSRC,
  output REGWRITE,
  output ReadRS,
  output ReadRT,
  output JR,
  output Shift
);

  wire functdecoder_1_jr, functdecoder_1_shift, uc_1_readregdecider;
  wire [1:0] functdecoder_1_readrt, uc_1_readrt;

  UC uc_1 (
    .UC5(in_1[5]), .UC4(in_1[4]), .UC3(in_1[3]), .UC2(in_1[2]), .REGDEST(REGDEST), .UC1(in_1[1]),
    .UC0(in_1[0]), .JAL(JAL), .JUMP(JUMP), .BNE(BNE), .BRANCH(BRANCH), .MEMTOREG(MEMTOREG),
    .ULAOP2(ALUOP[2]), .ULA0P1(ALUOP[1]), .ULA0P0(ALUOP[0]), .ULAOPSRC(ALUOP[3]), .MEM_WR(MEMWRITE),
    .ULASRC(ALUSRC), .WR(REGWRITE), .ReadRS(uc_1_readrt[1]), .ReadRT(uc_1_readrt[0]),
    .ReadRegDecider(uc_1_readregdecider));
  FunctDecoder functdecoder_1 (
    .FUNCT5(in_2[5]), .FUNCT4(in_2[4]), .FUNCT3(in_2[3]), .FUNCT2(in_2[2]), .FUNCT1(in_2[1]),
    .FUNCT0(in_2[0]), .JR(functdecoder_1_jr), .Shift(functdecoder_1_shift),
    .ReadRS(functdecoder_1_readrt[1]), .ReadRT(functdecoder_1_readrt[0]));
  Multiplexer #(.width(2), .enable("false")) multiplexer_1 (
    .in0(uc_1_readrt), .in1(functdecoder_1_readrt), .out({ReadRS, ReadRT}), .sel(uc_1_readregdecider));
  and and_1 (JR, ~in_1[0], ~in_1[1], ~in_1[2], ~in_1[3], ~in_1[4], ~in_1[5], functdecoder_1_jr);  // AND_Gate
  and and_2 (Shift, ~in_1[0], ~in_1[1], ~in_1[2], ~in_1[3], ~in_1[4], ~in_1[5], functdecoder_1_shift);  // AND_Gate
endmodule

// ALUCONTROL
module ALU_CONTROL (
  input  [3:0] in_1,
  input  [5:0] in_2,
  output [5:0] out_3
);

  wire [3:0] opula_1_ulaop0;
  wire [5:0] bit_extender_1_out, bit_extender_2_out;

  OPULA opula_1 (
    .ALUOP2(in_1[2]), .ALUOP1(in_1[1]), .ULAOP3(opula_1_ulaop0[3]), .ALUOP0(in_1[0]), .FUNC5(in_2[5]),
    .FUNC4(in_2[4]), .FUNC3(in_2[3]), .FUNC2(in_2[2]), .FUNC1(in_2[1]), .FUNC0(in_2[0]),
    .ULAOP2(opula_1_ulaop0[2]), .ULAOP1(opula_1_ulaop0[1]), .ULAOP0(opula_1_ulaop0[0]));
  assign bit_extender_1_out = {{2{opula_1_ulaop0[3]}}, opula_1_ulaop0};  // Bit_Extender bit_extender_1
  Multiplexer #(.width(6), .enable("false")) multiplexer_1 (
    .in0(bit_extender_1_out), .in1(bit_extender_2_out), .out(out_3), .sel(in_1[3]));
  assign bit_extender_2_out = {{3{in_1[2]}}, in_1[2:0]};  // Bit_Extender bit_extender_2
endmodule

// ID/EX
module REG_ID_EX (
  input  [31:0] JUMPADDR,
  input  JUMP,
  input  JR,
  input  Shift,
  input  RegDest,
  input  JAL,
  input  BNE,
  input  Branch,
  input  MemtoReg,
  input  [3:0] ALUOp,
  input  MemWrite,
  input  ALUSrc,
  input  RegWrite,
  input  ReadRS,
  input  ReadRT,
  input  Stall,
  input  [31:0] PC_4,
  input  [31:0] DATA_RS,
  input  [31:0] DATA_RT,
  input  [31:0] IMEXT,
  input  [4:0] RS,
  input  [4:0] RT,
  input  [4:0] RD,
  input  CLK,
  output [31:0] JUMPADDR_2,
  output JUMP_2,
  output JR_2,
  output Shift_2,
  output RegDest_2,
  output JAL_2,
  output BNE_2,
  output Branch_2,
  output MemtoReg_2,
  output [3:0] ALUOp_2,
  output MemWrite_2,
  output ALUSrc_2,
  output RegWrite_2,
  output ReadRS_2,
  output ReadRT_2,
  output [31:0] PC_4_2,
  output [31:0] DATA_RS_2,
  output [31:0] DATA_RT_2,
  output [31:0] IMEXT_2,
  output [4:0] RS_2,
  output [4:0] RT_2,
  output [4:0] RD_2
);

  wire multiplexer_1_out, multiplexer_2_out, multiplexer_3_out, multiplexer_4_out, multiplexer_5_out,
       multiplexer_6_out, multiplexer_7_out, multiplexer_8_out, multiplexer_9_out, multiplexer_10_out,
       multiplexer_11_out, multiplexer_12_out, multiplexer_13_out;

  Multiplexer #(.enable("false")) multiplexer_1 (.in0(JUMP), .in1(1'b0), .out(multiplexer_1_out), .sel(Stall));
  Multiplexer #(.enable("false")) multiplexer_2 (.in0(JR), .in1(1'b0), .out(multiplexer_2_out), .sel(Stall));
  Multiplexer #(.enable("false")) multiplexer_3 (.in0(Shift), .in1(1'b0), .out(multiplexer_3_out), .sel(Stall));
  Multiplexer #(.enable("false")) multiplexer_4 (.in0(RegDest), .in1(1'b0), .out(multiplexer_4_out), .sel(Stall));
  Multiplexer #(.enable("false")) multiplexer_5 (.in0(JAL), .in1(1'b0), .out(multiplexer_5_out), .sel(Stall));
  Multiplexer #(.enable("false")) multiplexer_6 (.in0(BNE), .in1(1'b0), .out(multiplexer_6_out), .sel(Stall));
  Multiplexer #(.enable("false")) multiplexer_7 (.in0(Branch), .in1(1'b0), .out(multiplexer_7_out), .sel(Stall));
  Multiplexer #(.enable("false")) multiplexer_8 (.in0(MemtoReg), .in1(1'b0), .out(multiplexer_8_out), .sel(Stall));
  Multiplexer #(.enable("false")) multiplexer_9 (.in0(MemWrite), .in1(1'b0), .out(multiplexer_9_out), .sel(Stall));
  Multiplexer #(.enable("false")) multiplexer_10 (.in0(ALUSrc), .in1(1'b0), .out(multiplexer_10_out), .sel(Stall));
  Multiplexer #(.enable("false")) multiplexer_11 (.in0(RegWrite), .in1(1'b0), .out(multiplexer_11_out), .sel(Stall));
  Multiplexer #(.enable("false")) multiplexer_12 (.in0(ReadRS), .in1(1'b0), .out(multiplexer_12_out), .sel(Stall));
  Multiplexer #(.enable("false")) multiplexer_13 (.in0(ReadRT), .in1(1'b0), .out(multiplexer_13_out), .sel(Stall));
  Register #(.width(32), .Select("low")) register_1 (.D(JUMPADDR), .Q(JUMPADDR_2), .clk(CLK));  // open: en, clr
  Register #(.width(1), .Select("low")) register_2 (.D(multiplexer_1_out), .Q(JUMP_2), .clk(CLK));  // open: en, clr
  Register #(.width(1), .Select("low")) register_3 (.D(multiplexer_2_out), .Q(JR_2), .clk(CLK));  // open: en, clr
  Register #(.width(1), .Select("low")) register_4 (.D(multiplexer_3_out), .Q(Shift_2), .clk(CLK));  // open: en, clr
  Register #(.width(1), .Select("low")) register_5 (.D(multiplexer_4_out), .Q(RegDest_2), .clk(CLK));  // open: en, clr
  Register #(.width(1), .Select("low")) register_6 (.D(multiplexer_5_out), .Q(JAL_2), .clk(CLK));  // open: en, clr
  Register #(.width(1), .Select("low")) register_7 (.D(multiplexer_6_out), .Q(BNE_2), .clk(CLK));  // open: en, clr
  Register #(.width(1), .Select("low")) register_8 (.D(multiplexer_7_out), .Q(Branch_2), .clk(CLK));  // open: en, clr
  Register #(.width(1), .Select("low")) register_9 (.D(multiplexer_8_out), .Q(MemtoReg_2), .clk(CLK));  // open: en, clr
  Register #(.width(4), .Select("low")) register_10 (.D(ALUOp), .Q(ALUOp_2), .clk(CLK));  // open: en, clr
  Register #(.width(1), .Select("low")) register_11 (
    .D(multiplexer_9_out), .Q(MemWrite_2), .clk(CLK));  // open: en, clr
  Register #(.width(1), .Select("low")) register_12 (.D(multiplexer_10_out), .Q(ALUSrc_2), .clk(CLK));  // open: en, clr
  Register #(.width(1), .Select("low")) register_13 (
    .D(multiplexer_11_out), .Q(RegWrite_2), .clk(CLK));  // open: en, clr
  Register #(.width(1), .Select("low")) register_14 (.D(multiplexer_12_out), .Q(ReadRS_2), .clk(CLK));  // open: en, clr
  Register #(.width(1), .Select("low")) register_15 (.D(multiplexer_13_out), .Q(ReadRT_2), .clk(CLK));  // open: en, clr
  Register #(.width(32), .Select("low")) register_16 (.D(PC_4), .Q(PC_4_2), .clk(CLK));  // open: en, clr
  Register #(.width(32), .Select("low")) register_17 (.D(DATA_RS), .Q(DATA_RS_2), .clk(CLK));  // open: en, clr
  Register #(.width(32), .Select("low")) register_18 (.D(DATA_RT), .Q(DATA_RT_2), .clk(CLK));  // open: en, clr
  Register #(.width(32), .Select("low")) register_19 (.D(IMEXT), .Q(IMEXT_2), .clk(CLK));  // open: en, clr
  Register #(.width(5), .Select("low")) register_20 (.D(RS), .Q(RS_2), .clk(CLK));  // open: en, clr
  Register #(.width(5), .Select("low")) register_21 (.D(RT), .Q(RT_2), .clk(CLK));  // open: en, clr
  Register #(.width(5), .Select("low")) register_22 (.D(RD), .Q(RD_2), .clk(CLK));  // open: en, clr
endmodule

// IF/ID
module REG_IF_ID (
  input  [31:0] in_1,
  input  [31:0] in_2,
  input  Enable,
  input  CLK,
  output [31:0] out_5,
  output [31:0] out_6
);

  Register #(.width(32), .Select("low")) register_1 (.D(in_1), .en(Enable), .Q(out_5), .clk(CLK));  // open: clr
  Register #(.width(32), .Select("low")) register_2 (.D(in_2), .en(Enable), .Q(out_6), .clk(CLK));  // open: clr
endmodule

// EX/MEM
module REG_EX_MEM (
  input  [31:0] PC_4,
  input  BNE,
  input  BRANCH,
  input  JAL,
  input  MEMTOREG,
  input  MEMORY_WRITE,
  input  REGWRITE,
  input  [31:0] BRANCH_ADDRESS,
  input  zero,
  input  [31:0] ALU_OUT,
  input  [31:0] DATA_RT,
  input  [4:0] WRITE_REGISTER,
  input  CLK,
  output [31:0] PC_4_2,
  output BNE_2,
  output BRANCH_2,
  output JAL_2,
  output MEMTOREG_2,
  output MEMORY_WRITE_2,
  output REGWRITE_2,
  output [31:0] BRANCH_ADDRESS_2,
  output zero_2,
  output [31:0] ALU_OUT_2,
  output [31:0] DATA_RT_2,
  output [4:0] WRITE_REGISTER_2
);

  Register #(.width(32), .Select("low")) register_1 (.D(PC_4), .Q(PC_4_2), .clk(CLK));  // open: en, clr
  Register #(.width(1), .Select("low")) register_2 (.D(BNE), .Q(BNE_2), .clk(CLK));  // open: en, clr
  Register #(.width(1), .Select("low")) register_3 (.D(BRANCH), .Q(BRANCH_2), .clk(CLK));  // open: en, clr
  Register #(.width(1), .Select("low")) register_4 (.D(JAL), .Q(JAL_2), .clk(CLK));  // open: en, clr
  Register #(.width(1), .Select("low")) register_5 (.D(MEMTOREG), .Q(MEMTOREG_2), .clk(CLK));  // open: en, clr
  Register #(.width(1), .Select("low")) register_6 (.D(MEMORY_WRITE), .Q(MEMORY_WRITE_2), .clk(CLK));  // open: en, clr
  Register #(.width(1), .Select("low")) register_7 (.D(REGWRITE), .Q(REGWRITE_2), .clk(CLK));  // open: en, clr
  Register #(.width(32), .Select("low")) register_8 (
    .D(BRANCH_ADDRESS), .Q(BRANCH_ADDRESS_2), .clk(CLK));  // open: en, clr
  Register #(.width(1), .Select("low")) register_9 (.D(zero), .Q(zero_2), .clk(CLK));  // open: en, clr
  Register #(.width(32), .Select("low")) register_10 (.D(ALU_OUT), .Q(ALU_OUT_2), .clk(CLK));  // open: en, clr
  Register #(.width(32), .Select("low")) register_11 (.D(DATA_RT), .Q(DATA_RT_2), .clk(CLK));  // open: en, clr
  Register #(.width(5), .Select("low")) register_12 (
    .D(WRITE_REGISTER), .Q(WRITE_REGISTER_2), .clk(CLK));  // open: en, clr
endmodule

// MEM/WB
module REG_MEM_WB (
  input  [31:0] PC_4,
  input  JAL,
  input  REG_WRITE,
  input  MEMTOREG,
  input  [31:0] MEM_OUT,
  input  [31:0] ALU_OUT,
  input  [4:0] WRITE_REGISTER,
  input  CLK,
  output [31:0] PC_4_2,
  output JAL_2,
  output REG_WRITE_2,
  output MEMTOREG_2,
  output [31:0] MEM_OUT_2,
  output [31:0] ALU_OUT_2,
  output [4:0] WRITE_REGISTER_2
);

  Register #(.width(32), .Select("low")) register_1 (.D(PC_4), .Q(PC_4_2), .clk(CLK));  // open: en, clr
  Register #(.width(1), .Select("low")) register_2 (.D(JAL), .Q(JAL_2), .clk(CLK));  // open: en, clr
  Register #(.width(1), .Select("low")) register_3 (.D(REG_WRITE), .Q(REG_WRITE_2), .clk(CLK));  // open: en, clr
  Register #(.width(1), .Select("low")) register_4 (.D(MEMTOREG), .Q(MEMTOREG_2), .clk(CLK));  // open: en, clr
  Register #(.width(32), .Select("low")) register_5 (.D(MEM_OUT), .Q(MEM_OUT_2), .clk(CLK));  // open: en, clr
  Register #(.width(32), .Select("low")) register_6 (.D(ALU_OUT), .Q(ALU_OUT_2), .clk(CLK));  // open: en, clr
  Register #(.width(5), .Select("low")) register_7 (
    .D(WRITE_REGISTER), .Q(WRITE_REGISTER_2), .clk(CLK));  // open: en, clr
endmodule

module FunctDecoder (
  input  FUNCT5,
  input  FUNCT4,
  input  FUNCT3,
  input  FUNCT2,
  input  FUNCT1,
  input  FUNCT0,
  output JR,
  output Shift,
  output ReadRS,
  output ReadRT
);

  wire and_3_out, and_4_out, and_5_out, and_6_out, and_7_out, and_8_out, and_9_out, and_10_out, not_1_out,
       not_2_out, not_3_out, not_4_out, not_5_out, not_6_out, not_7_out, not_8_out, not_9_out, not_10_out,
       not_11_out, not_12_out, not_13_out, not_14_out, not_15_out, not_16_out, not_17_out, not_18_out,
       not_19_out, not_20_out, not_21_out, not_22_out, not_23_out, not_24_out, not_25_out, not_26_out,
       not_27_out, not_28_out, not_29_out, not_30_out, not_31_out, not_32_out, not_33_out, not_34_out,
       not_35_out, not_36_out;

  not not_1 (not_1_out, FUNCT5);
  not not_2 (not_2_out, FUNCT4);
  not not_3 (not_3_out, FUNCT2);
  not not_4 (not_4_out, FUNCT1);
  not not_5 (not_5_out, FUNCT0);
  not not_6 (not_6_out, FUNCT5);
  not not_7 (not_7_out, FUNCT4);
  not not_8 (not_8_out, FUNCT3);
  not not_9 (not_9_out, FUNCT2);
  not not_10 (not_10_out, FUNCT0);
  not not_11 (not_11_out, FUNCT5);
  not not_12 (not_12_out, FUNCT2);
  not not_13 (not_13_out, FUNCT0);
  not not_14 (not_14_out, FUNCT4);
  not not_15 (not_15_out, FUNCT3);
  not not_16 (not_16_out, FUNCT2);
  not not_17 (not_17_out, FUNCT0);
  not not_18 (not_18_out, FUNCT4);
  not not_19 (not_19_out, FUNCT2);
  not not_20 (not_20_out, FUNCT0);
  not not_21 (not_21_out, FUNCT4);
  not not_22 (not_22_out, FUNCT3);
  not not_23 (not_23_out, FUNCT1);
  not not_24 (not_24_out, FUNCT4);
  not not_25 (not_25_out, FUNCT3);
  not not_26 (not_26_out, FUNCT2);
  not not_27 (not_27_out, FUNCT0);
  not not_28 (not_28_out, FUNCT5);
  not not_29 (not_29_out, FUNCT2);
  not not_30 (not_30_out, FUNCT0);
  not not_31 (not_31_out, FUNCT4);
  not not_32 (not_32_out, FUNCT2);
  not not_33 (not_33_out, FUNCT0);
  not not_34 (not_34_out, FUNCT4);
  not not_35 (not_35_out, FUNCT3);
  not not_36 (not_36_out, FUNCT1);
  and and_1 (JR, not_1_out, not_2_out, FUNCT3, not_3_out, not_4_out, not_5_out);
  and and_2 (Shift, not_6_out, not_7_out, not_8_out, not_9_out, not_10_out);
  and and_3 (and_3_out, not_11_out, FUNCT4, FUNCT3, not_12_out, not_13_out);
  and and_4 (and_4_out, FUNCT5, not_14_out, not_15_out, not_16_out, not_17_out);
  and and_5 (and_5_out, FUNCT5, not_18_out, not_19_out, FUNCT1, not_20_out);
  and and_6 (and_6_out, FUNCT5, not_21_out, not_22_out, FUNCT2, not_23_out);
  and and_7 (and_7_out, not_24_out, not_25_out, not_26_out, not_27_out);
  and and_8 (and_8_out, not_28_out, FUNCT4, FUNCT3, not_29_out, not_30_out);
  and and_9 (and_9_out, FUNCT5, not_31_out, not_32_out, FUNCT1, not_33_out);
  and and_10 (and_10_out, FUNCT5, not_34_out, not_35_out, FUNCT2, not_36_out);
  or or_1 (ReadRS, and_3_out, and_4_out, and_5_out, and_6_out);
  or or_2 (ReadRT, and_7_out, and_8_out, and_9_out, and_10_out);
endmodule

module HazardDetector (
  input  RegRead,
  input  RegWrite,
  input  [4:0] RegD,
  input  [4:0] Reg_num,
  output Hazard
);

  wire comparator_1_eq, comparator_2_eq, not_1_out;

  not not_1 (not_1_out, comparator_1_eq);
  Comparator #(.width(5)) comparator_1 (.a({5{1'b0}}), .b(RegD), .eq(comparator_1_eq));  // open: gt, lt
  Comparator #(.width(5)) comparator_2 (.a(RegD), .b(Reg_num), .eq(comparator_2_eq));  // open: gt, lt
  and and_1 (Hazard, RegRead, RegWrite, not_1_out, comparator_2_eq);
endmodule

// Hazard Unit
module HazardUnit (
  input  [4:0] RS_EX,
  input  [4:0] RT_EX,
  input  [4:0] RegDMem,
  input  [4:0] RegDWb,
  input  ReadRS_EX,
  input  ReadRT_EX,
  input  RegWriteMem,
  input  RegWriteWb,
  input  [4:0] RS_ID,
  input  [4:0] RT_ID,
  input  ReadRS_ID,
  input  ReadRT_ID,
  input  isLW,
  output [1:0] RSOutput,
  output [1:0] RTOutput,
  output StallID,
  output Bubble,
  output StallPC
);

  wire hazarddetector_1_hazard, hazarddetector_2_hazard, hazarddetector_3_hazard, hazarddetector_4_hazard,
       hazarddetector_5_hazard, hazarddetector_6_hazard, or_1_out;
  wire [1:0] multiplexer_1_out, multiplexer_3_out;

  HazardDetector hazarddetector_1 (
    .RegRead(ReadRS_ID), .RegWrite(isLW), .RegD(RT_EX), .Reg_num(RS_ID), .Hazard(hazarddetector_1_hazard));
  HazardDetector hazarddetector_2 (
    .RegRead(ReadRT_ID), .RegWrite(isLW), .RegD(RT_EX), .Reg_num(RT_ID), .Hazard(hazarddetector_2_hazard));
  HazardDetector hazarddetector_3 (
    .RegRead(ReadRS_EX), .RegWrite(RegWriteWb), .RegD(RegDWb), .Reg_num(RS_EX),
    .Hazard(hazarddetector_3_hazard));
  HazardDetector hazarddetector_4 (
    .RegRead(ReadRS_EX), .RegWrite(RegWriteMem), .RegD(RegDMem), .Reg_num(RS_EX),
    .Hazard(hazarddetector_4_hazard));
  HazardDetector hazarddetector_5 (
    .RegRead(ReadRT_EX), .RegWrite(RegWriteWb), .RegD(RegDWb), .Reg_num(RT_EX),
    .Hazard(hazarddetector_5_hazard));
  HazardDetector hazarddetector_6 (
    .RegRead(ReadRT_EX), .RegWrite(RegWriteMem), .RegD(RegDMem), .Reg_num(RT_EX),
    .Hazard(hazarddetector_6_hazard));
  or or_1 (or_1_out, hazarddetector_1_hazard, hazarddetector_2_hazard);
  Multiplexer #(.width(2), .enable("false")) multiplexer_1 (
    .in0(2'b00), .in1(2'b10), .out(multiplexer_1_out), .sel(hazarddetector_3_hazard));
  Multiplexer #(.width(2), .enable("false")) multiplexer_2 (
    .in0(multiplexer_1_out), .in1(2'b01), .out(RSOutput), .sel(hazarddetector_4_hazard));
  Multiplexer #(.width(2), .enable("false")) multiplexer_3 (
    .in0(2'b00), .in1(2'b10), .out(multiplexer_3_out), .sel(hazarddetector_5_hazard));
  Multiplexer #(.width(2), .enable("false")) multiplexer_4 (
    .in0(multiplexer_3_out), .in1(2'b01), .out(RTOutput), .sel(hazarddetector_6_hazard));
  and and_1 (Bubble, isLW, or_1_out);

  assign StallID = Bubble;
  assign StallPC = Bubble;

  // Notes on the sheet:
  //   Stall
  //   Forwarding
endmodule

module BranchDecider (
  input  BEQ,
  input  BNE,
  input  EQ,
  output Branch
);

  wire and_1_out, and_2_out;

  and and_1 (and_1_out, EQ, BEQ);
  and and_2 (and_2_out, BNE, ~EQ);  // AND_Gate
  or or_1 (Branch, and_1_out, and_2_out);
endmodule
